# Fritzing sketch schema OLED I2C 128x64 ssd1306 (saved by Fritzing 0.9.3b)
breadboards: 1

parts:
  Composant1 = Arduino Uno (Rev3)
  OLED_I2C1 = OLED 128x64 I2C Monochrome Display

nets:
  N1: Composant1.A4/SDA, OLED_I2C1.SDA
  N2: Composant1.A5/SCL, OLED_I2C1.SCK
  3V3: Composant1.3V3, OLED_I2C1.VDD
  GND: Composant1.GND, OLED_I2C1.GND
